# Fritzing sketch TDA1308_Test (saved by Fritzing 0.9.2b)
breadboards: 1

parts:
  U1 = mystery part, 8 pins [chip_label=TDA1308]
  R1 = Resistor [tolerance=±5% resistance=3.3k package=THT]
  R2 = Resistor [tolerance=±5% resistance=3.3k package=THT]
  C1 = Ceramic Capacitor [capacitance=100nF package="100 mil [THT, multilayer]"]
  C2 = Electrolytic Capacitor [capacitance=1µF package="100 mil [THT, electrolytic]"]
  R3 = Resistor [tolerance=±5% resistance=10k package=THT]
  R4 = Resistor [tolerance=±5% resistance=10k package=THT]
  C3 = Electrolytic Capacitor [capacitance=1µF package="100 mil [THT, electrolytic]"]
  R5 = Resistor [tolerance=±5% resistance=33 package=THT]
  R6 = Resistor [tolerance=±5% resistance=3.3k package=THT]
  R7 = Resistor [tolerance=±5% resistance=3.3k package=THT]
  C4 = Ceramic Capacitor [capacitance=100nF package="100 mil [THT, multilayer]"]
  C5 = Electrolytic Capacitor [capacitance=1µF package="100 mil [THT, electrolytic]"]
  R8 = Resistor [tolerance=±5% resistance=33 package=THT]
  VCC1 = Battery
  C6 = Ceramic Capacitor [capacitance=100nF package="100 mil [THT, multilayer]"]
  C7 = Electrolytic Capacitor [capacitance=1µF package="100 mil [THT, electrolytic]"]

nets:
  N1: U1.pin1, R1.Pin_1, C3.+
  N2: U1.pin2, R1.Pin_0, R2.Pin_1
  N3: U1.pin3, U1.pin5, C2.+, R3.Pin_1, R4.Pin_0
  N4: U1.pin4, C2.-, R4.Pin_1, R5.Pin_1, R8.Pin_1, VCC1.-, C6.1, C7.-
  N5: U1.pin6, R6.Pin_0, R7.Pin_1
  N6: U1.pin7, R6.Pin_1, C5.+
  N7: U1.pin8, R3.Pin_0, VCC1.+, C6.0, C7.+
  N8: R2.Pin_0, C1.1
  N9: C3.-, R5.Pin_0
  N10: R7.Pin_0, C4.1
  N11: C5.-, R8.Pin_0

notes:
  INA
  VSS
  VDD/2
  VDD/2
  VDD
  VOUTA
  INB
  OUTB
  5V
