# Fritzing sketch TPA1308_InvAmp_2ch (saved by Fritzing 0.9.2b)
breadboards: 1

parts:
  U1 = mystery part, 8 pins [chip_label=TDA1308]
  R1 = Resistor [tolerance=±5% resistance=12k package=THT]
  C1 = Ceramic Capacitor [capacitance=100nF package="100 mil [THT, multilayer]"]
  C2 = Ceramic Capacitor [capacitance=100nF package="100 mil [THT, multilayer]"]
  R4 = Rotary Potentiometer (Small) [maximum_resistance=100kΩ package=THT]
  TRS1 = Audio Jack (TRS) 3.5mm [package="4Ucon 08780 [THT]"]
  C3 = Electrolytic Capacitor [capacitance=1µF package="100 mil [THT, electrolytic]"]
  C4 = Electrolytic Capacitor [capacitance=1µF package="100 mil [THT, electrolytic]"]
  VCC1 = Battery
  VCC2 = Battery
  R6 = Resistor [tolerance=±5% resistance=47k package=THT]
  R7 = Rotary Potentiometer (Small) [maximum_resistance=100kΩ package=THT]
  R8 = Resistor [tolerance=±5% resistance=47k package=THT]
  R9 = Resistor [tolerance=±5% resistance=12k package=THT]
  C5 = Ceramic Capacitor [capacitance=100nF package="100 mil [THT, multilayer]"]
  TRS2 = Audio Jack (TRS) 3.5mm [package="4Ucon 08780 [THT]"]

nets:
  N1: U1.pin1, R6.Pin_1, TRS2.Tip
  N2: U1.pin2, R1.Pin_1, R6.Pin_0
  N3: U1.pin3, U1.pin5, C1.1, R4.leg1, TRS1.Sleeve, C3.-, C4.+, VCC1.-, VCC2.+, R7.leg1, TRS2.Sleeve
  N4: U1.pin4, C4.-, VCC2.-
  N5: U1.pin6, R8.Pin_0, R9.Pin_1
  N6: U1.pin7, R8.Pin_1, TRS2.Ring
  N7: U1.pin8, C1.0, C3.+, VCC1.+
  N8: R1.Pin_0, C2.1
  N9: C2.0, R4.wiper
  N10: R4.leg2, TRS1.Tip
  N11: TRS1.Ring, R7.leg2
  N12: R7.wiper, C5.0
  N13: R9.Pin_0, C5.1

notes:
  GND
  V+
  V-
  GND
  Input
  Output
