# Fritzing sketch TPA1308_NoInvAmp (saved by Fritzing 0.9.2b)
breadboards: 1

parts:
  U1 = mystery part, 8 pins [chip_label=TDA1308]
  R1 = Resistor [tolerance=±5% resistance=47k package=THT]
  C1 = Ceramic Capacitor [capacitance=100nF package="100 mil [THT, multilayer]"]
  R3 = Resistor [tolerance=±5% resistance=100k package=THT]
  C2 = Ceramic Capacitor [capacitance=100nF package="100 mil [THT, multilayer]"]
  R4 = Rotary Potentiometer (Small) [maximum_resistance=100kΩ package=THT]
  TRS1 = Audio Jack (TRS) 3.5mm [package="4Ucon 08780 [THT]"]
  C3 = Electrolytic Capacitor [capacitance=1µF package="100 mil [THT, electrolytic]"]
  C4 = Electrolytic Capacitor [capacitance=1µF package="100 mil [THT, electrolytic]"]
  VCC1 = Battery
  VCC2 = Battery
  R5 = Resistor [tolerance=±5% resistance=33 package=THT]
  R6 = Resistor [tolerance=±5% resistance=15k package=THT]

nets:
  N1: U1.pin1, R1.Pin_0, R5.Pin_0
  N2: U1.pin2, R1.Pin_1, R6.Pin_0
  N3: U1.pin3, R3.Pin_0, C2.1
  N4: U1.pin4, R3.Pin_1, C4.-, VCC2.-
  N5: U1.pin5, C1.0, R4.leg1, TRS1.Sleeve, C3.-, C4.+, VCC1.-, VCC2.+, R5.Pin_1, R6.Pin_1
  N6: U1.pin6, U1.pin7
  N7: U1.pin8, C1.1, C3.+, VCC1.+
  N8: C2.0, R4.wiper
  N9: R4.leg2, TRS1.Tip

notes:
  OUT-L
